// Logisim project fon_neiman_2.circ as structural Verilog: 1 circuit, main circuit main
module main (
  output [7:0] out_1
);

  wire and_1_out, and_2_out, clock_1_out, not_1_out, not_2_out, reset_out;
  wire [3:0] addres_q, counter_1_q, instruct_q, multiplexer_1_out;
  wire [7:0] adder_1_out, multiplexer_2_out, ram_1_data, temp_q;

  Button reset (.out(reset_out));
  Clock clock_1 (.out(clock_1_out));
  Counter #(.width(4), .max('hf)) counter_1 (
    .Q(counter_1_q), .clk(clock_1_out), .clr(reset_out));  // open: load, D, count, carry
  not not_1 (not_1_out, clock_1_out);
  Multiplexer #(.width(4)) multiplexer_1 (
    .in0(counter_1_q), .in1(addres_q), .out(multiplexer_1_out), .sel(not_1_out));  // open: en
  and and_1 (and_1_out, clock_1_out, instruct_q[1]);
  // Probe on ram_1_data
  RAM #(.addrWidth(4), .bus("separate")) ram_1 (
    .addr(multiplexer_1_out), .din(out_1), .data(ram_1_data), .clk(and_1_out));  // open: str, sel, ld, clr
  Register #(.trigger("falling")) temp (.D(ram_1_data), .Q(temp_q), .clk(and_2_out), .clr(reset_out));  // open: en
  // Probe on ram_1_data[3:0]
  // Probe on temp_q
  // Probe on ram_1_data[7:4]
  Register #(.width(4)) addres (.D(ram_1_data[3:0]), .Q(addres_q), .clk(not_1_out), .clr(reset_out));  // open: en
  Adder adder_1 (.a(out_1), .b(temp_q), .out(adder_1_out));  // open: cin, cout
  Register #(.width(4)) instruct (.D(ram_1_data[7:4]), .Q(instruct_q), .clk(not_1_out), .clr(reset_out));  // open: en
  Multiplexer #(.width(8)) multiplexer_2 (
    .in0(adder_1_out), .in1(temp_q), .out(multiplexer_2_out), .sel(instruct_q[2]));  // open: en
  and and_2 (and_2_out, instruct_q[0], not_1_out);
  not not_2 (not_2_out, not_1_out);
  Register #(.trigger("falling")) accum (
    .D(multiplexer_2_out), .Q(out_1), .clk(not_2_out), .clr(reset_out));  // open: en
endmodule
