// Logisim project fon_neiman_3.circ as structural Verilog: 1 circuit, main circuit main
module main (
  input  [7:0] in_1,
  output [7:0] out_2,
  output [7:0] out_3,
  output out_4
);

  wire and_1_out, and_2_out, and_3_out, clock_1_out, clock_2_out, clock_3_out, not_1_out, not_2_out,
       not_3_out, not_4_out, not_6_out, reset_out;
  wire [3:0] address_q, counter_1_q, counter_2_q, instruction_q, multiplexer_1_out;
  wire [7:0] adder_1_out, multiplexer_2_out, ram_1_data, ram_2_data, temp_q;

  Button reset (.out(reset_out));
  Counter #(.width(4), .max('hf)) counter_1 (
    .load(instruction_q[3]), .D(address_q), .count(not_1_out), .Q(counter_1_q), .clk(clock_1_out),
    .clr(reset_out));  // open: carry
  not not_1 (not_1_out, instruction_q[3]);
  Clock clock_1 (.out(clock_1_out));
  Clock clock_2 (.out(clock_2_out));
  not not_2 (not_2_out, ram_2_data[7]);
  Clock clock_3 (.out(clock_3_out));
  // Probe on multiplexer_1_out
  Multiplexer #(.width(4)) multiplexer_1 (
    .in0(counter_1_q), .in1(address_q), .out(multiplexer_1_out), .sel(not_3_out));  // open: en
  not not_3 (not_3_out, clock_1_out);
  not not_4 (not_4_out, clock_2_out);
  Counter #(.width(4), .max('hf)) counter_2 (
    .load(ram_2_data[7]), .D(ram_2_data[3:0]), .count(not_2_out), .Q(counter_2_q), .clk(clock_3_out));  // open: carry, clr
  not not_5 (out_4, clock_3_out);
  and and_1 (and_1_out, clock_1_out, instruction_q[1]);
  and and_2 (and_2_out, clock_2_out, not_4_out);
  RAM #(.addrWidth(4), .bus("separate")) ram_1 (
    .addr(multiplexer_1_out), .din(out_2), .data(ram_1_data), .clk(and_1_out));  // open: str, sel, ld, clr
  // Probe on ram_1_data
  RAM #(.addrWidth(4), .bus("separate")) ram_2 (
    .addr(counter_2_q), .data(ram_2_data));  // open: din, str, sel, clk, ld, clr
  Register #(.trigger("falling")) temp (.D(ram_1_data), .Q(temp_q), .clk(and_3_out), .clr(reset_out));  // open: en
  Register #(.width(4)) address (.D(ram_1_data[3:0]), .Q(address_q), .clk(not_3_out), .clr(reset_out));  // open: en
  Register register_1 (.D(in_1), .Q(out_3), .clk(and_2_out));  // open: en, clr
  // Probe on ram_2_data[3:0]
  Register #(.width(4)) instruction (
    .D(ram_1_data[7:4]), .Q(instruction_q), .clk(not_3_out), .clr(reset_out));  // open: en
  // Probe on ram_2_data[7:4]
  Multiplexer #(.width(8)) multiplexer_2 (
    .in0(adder_1_out), .in1(temp_q), .out(multiplexer_2_out), .sel(instruction_q[2]));  // open: en
  Adder adder_1 (.a(out_2), .b(temp_q), .out(adder_1_out));  // open: cin, cout
  // Probe on multiplexer_2_out
  and and_3 (and_3_out, instruction_q[0], not_3_out);
  Register #(.trigger("falling")) accamulator (
    .D(multiplexer_2_out), .Q(out_2), .clk(not_6_out), .clr(reset_out));  // open: en
  not not_6 (not_6_out, not_3_out);

  // Notes on the sheet:
  //   Аномальная работа регистра (Регистр записывает входящее число при сигнале 0 от логического вентиля (И))
  //   Реализация безусловного перехода
endmodule
