// Logisim project harvard_architecture.circ as structural Verilog: 1 circuit, main circuit main
module main (
  output [7:0] out_1
);

  wire and_1_out, button_1_out, button_2_out, clock_1_out, not_1_out;
  wire [1:0] ram_1_data;
  wire [3:0] counter_1_q;
  wire [7:0] adder_1_out, ram_2_data;

  Button button_1 (.out(button_1_out));
  Clock clock_1 (.out(clock_1_out));
  Counter #(.width(4), .max('hf)) counter_1 (
    .Q(counter_1_q), .clk(clock_1_out), .clr(button_1_out));  // open: load, D, count, carry
  not not_1 (not_1_out, clock_1_out);
  RAM #(.addrWidth(4), .dataWidth(2), .bus("separate")) ram_1 (
    .addr(counter_1_q), .data(ram_1_data));  // open: din, str, sel, clk, ld, clr
  RAM #(.addrWidth(4), .bus("separate")) ram_2 (
    .addr(counter_1_q), .din(out_1), .data(ram_2_data), .clk(ram_1_data[1]));  // open: str, sel, ld, clr
  Adder adder_1 (.a(out_1), .b(ram_2_data), .out(adder_1_out));  // open: cin, cout
  and and_1 (and_1_out, ram_1_data[0], not_1_out);
  Register register_1 (.D(adder_1_out), .Q(out_1), .clk(and_1_out), .clr(button_2_out));  // open: en
  Button button_2 (.out(button_2_out));
endmodule
