// Logisim project tact_save_in_memory_and_offset_at_the_same_time.circ as structural Verilog: 1 circuit, main circuit main
module main (
  input  [7:0] in_1,
  output [7:0] out_2
);

  wire clock_1_out;
  wire [3:0] counter_1_q;

  Clock clock_1 (.out(clock_1_out));
  Counter #(.width(4), .max('hf)) counter_1 (.Q(counter_1_q), .clk(clock_1_out));  // open: load, D, count, carry, clr
  RAM #(.addrWidth(4), .bus("separate")) ram_1 (
    .addr(counter_1_q), .din(in_1), .data(out_2), .clk(clock_1_out));  // open: str, sel, ld, clr

  // Notes on the sheet:
  //   сохранение в ячейку памяти и смешение counter'а памяти в один такт
endmodule
